# Fritzing sketch data_meter (saved by Fritzing 0.9.2b)
breadboards: 1

parts:
  Arduino = Arduino Pro Mini v13
  HC-05 = Bluetooth HC-05 Macho
  MPU6050 = MPU-6050 Board GY-521 [form="♀ (female)" package=THT]
  J1 = Basic Force Sensing Resistor (FSR) [package=THT]
  R1 = Resistor [tolerance=±5% resistance=220 package=THT]

nets:
  N1: Arduino.DTR, Arduino.D0/TX
  GND: Arduino.GND, HC-05.GND, MPU6050.pin2, R1.Pin_0
  N2: Arduino.A4, MPU6050.pin3
  N3: Arduino.A5, MPU6050.pin4
  VCC: Arduino.VCC, HC-05.VCC, MPU6050.pin1, J1.pin_1
  N4: Arduino.A0, J1.pin_0, R1.Pin_1
  N5: Arduino.D3_PWM, HC-05.RXD
  N6: Arduino.D2, HC-05.TXD

custom parts:
  MPU-6050 Board GY-521: Acelerometro y Giroscopio MPU-6050 Board GY-521
